// Logisim project cpu.circ as structural Verilog: 2 circuits, main circuit ControlUnit
module ControlUnit (
  input  [3:0] Opcode,
  input  Z,
  input  N,
  input  C,
  input  V,
  output FLAG_WE,
  output Register_WE,
  output RAM_WE,
  output ProgCount_Load,
  output STOP,
  output [1:0] outputDevice
);

  wire and_1_out, nor_1_out, not_1_out, not_2_out;

  nor nor_1 (nor_1_out, Opcode[2], Opcode[3]);
  and and_1 (and_1_out, Opcode[0], Opcode[1]);
  and and_2 (FLAG_WE, nor_1_out, not_1_out);
  not not_1 (not_1_out, and_1_out);
  Multiplexer #(.select(4)) multiplexer_1 (
    .in0(1'b1), .in1(1'b1), .in2(1'b1), .in3(1'b1), .in4(1'b1), .in5(1'b0), .in6(1'b0), .in7(1'b0),
    .in8(1'b0), .in9(1'b0), .in10(1'b0), .in11(1'b0), .in12(1'b0), .in13(1'b0), .in14(1'b0), .in15(1'b0),
    .out(Register_WE), .sel(Opcode));
  and and_3 (RAM_WE, Opcode[0], ~Opcode[1], Opcode[2], ~Opcode[3]);  // AND_Gate
  not not_2 (not_2_out, Z);
  Multiplexer #(.select(4)) multiplexer_2 (
    .in0(1'b0), .in1(1'b0), .in2(1'b0), .in3(1'b0), .in4(1'b0), .in5(1'b0), .in6(1'b1), .in7(Z),
    .in8(not_2_out), .in9(N), .in10(V), .in11(C), .in12(1'b0), .in13(1'b0), .in14(1'b0), .in15(1'b0),
    .out(ProgCount_Load), .sel(Opcode));
  and and_4 (STOP, Opcode[0], Opcode[1], Opcode[2], Opcode[3]);
  Multiplexer #(.select(4), .width(2)) multiplexer_3 (
    .in0(2'b01), .in1(2'b01), .in2(2'b01), .in3(2'b10), .in4(2'b11), .in5(2'b00), .in6(2'b00), .in7(2'b00),
    .in8(2'b00), .in9(2'b00), .in10(2'b00), .in11(2'b00), .in12(2'b00), .in13(2'b00), .in14(2'b00),
    .in15(2'b00), .out(outputDevice), .sel(Opcode));

  // Other names for the same wires on the sheet: OPC[3:0] = Opcode
endmodule

module main (
);

  wire CLK;
  wire [15:0] instructionrom_1_instruction;

  Clock u_CLK (.out(CLK));
  instructionROM instructionrom_1 (.Instruction(instructionrom_1_instruction));  // open: CLK, Jump_Addr, PC_Load, Reset
  ControlUnit controlunit_1 (.Opcode(instructionrom_1_instruction[3:0]));  // open: Z, N, C, V, FLAG_WE, Register_WE, RAM_WE, ProgCount_Load, STOP, outputDevice
  // FLAGS_regs flags_regs_1: pin names not known
endmodule
