// Logisim project memoryProgramCounter.circ as structural Verilog: 2 circuits, main circuit programCounter
module programCounter (
  input  CLK,
  input  [11:0] Jump_Addr,
  input  PC_Load,
  input  Reset,
  output [11:0] Line
);

  wire fulladder1_1_cout, fulladder1_2_cout, fulladder1_3_cout, fulladder8_1_cout;
  wire [11:0] fulladder8_1_sum, multiplexer_1_out;

  Register #(.width(12)) register_1 (.D(multiplexer_1_out), .en(CLK), .clk(CLK), .Q(Line), .clr(Reset));
  Multiplexer #(.width(12)) multiplexer_1 (
    .in0(fulladder8_1_sum), .in1(Jump_Addr), .out(multiplexer_1_out), .sel(PC_Load));
  FullAdder8 fulladder8_1 (
    .b(Line[7:0]), .cin(1'b1), .cout(fulladder8_1_cout), .sum(fulladder8_1_sum[7:0]));  // open: a, cout6
  FullAdder1 fulladder1_1 (
    .a(Line[8]), .cin(fulladder8_1_cout), .cout(fulladder1_1_cout), .s(fulladder8_1_sum[8]));  // open: b
  FullAdder1 fulladder1_2 (
    .a(Line[9]), .cin(fulladder1_1_cout), .cout(fulladder1_2_cout), .s(fulladder8_1_sum[9]));  // open: b
  FullAdder1 fulladder1_3 (
    .a(Line[10]), .cin(fulladder1_2_cout), .cout(fulladder1_3_cout), .s(fulladder8_1_sum[10]));  // open: b
  FullAdder1 fulladder1_4 (.a(Line[11]), .cin(fulladder1_3_cout), .s(fulladder8_1_sum[11]));  // open: b, cout
endmodule

module memory (
);

  wire [11:0] programcounter_1_line;

  ROM #(.addrWidth(12)) ProgramMemory (.addr(programcounter_1_line));  // open: data
  programCounter programcounter_1 (.Line(programcounter_1_line));  // open: CLK, Jump_Addr, PC_Load, Reset
endmodule
