// Logisim project registers.circ as structural Verilog
module main_regs (
  input  CLK,
  input  WE,
  input  [2:0] Rd,
  input  [2:0] Rs1,
  input  [2:0] Rs2,
  input  [7:0] InputData
);

  Register r0 (.D({8{1'b0}}), .clk(CLK));  // open: en, Q, clr
  Register r1 (.D(InputData), .clk(CLK));  // open: en, Q, clr
  Register r2 (.D(InputData), .clk(CLK));  // open: en, Q, clr
  Register r3 (.D(InputData), .clk(CLK));  // open: en, Q, clr
  Register r4 (.D(InputData), .clk(CLK));  // open: en, Q, clr
  Register r5 (.D(InputData), .clk(CLK));  // open: en, Q, clr
  Register r6 (.D(InputData), .clk(CLK));  // open: en, Q, clr
  Register r7 (.D(InputData), .clk(CLK));  // open: en, Q, clr

  // Other names for the same wires on the sheet: clock = CLK; data[7:0] = InputData
endmodule
